# Fritzing sketch PressureSensorLogger (saved by Fritzing 0.9.1b)
breadboards: 1

parts:
  Part1 = Arduino Nano (Rev3.0) (ICSP)
  BMP1 = BMP085 Breakout
  microSD1 = MicroSD Breakout

nets:
  GND: Part1.GND, BMP1.GND, microSD1.GND
  N1: Part1.D7, microSD1.CS
  N2: Part1.D11/MOSI, microSD1.DI
  N3: Part1.D12/MISO, microSD1.DO
  5V: Part1.5V, BMP1.VIN, microSD1.5V
  N4: Part1.A5, BMP1.SCL
  N5: Part1.A4, BMP1.SDA
  N6: Part1.D13/SCK, microSD1.CLK

custom parts:
  BMP085 Breakout: A breakout for the BMP085 barometric pressure and temperature sensor
  MicroSD Breakout: 5V-ready microSD Breakout with Level Shifter
